# Fritzing sketch Reader24ch_PB_Layout (saved by Fritzing 0.9.3b)
perfboards: 1

parts:
  J1 = double row male pin header, 8 pins [form="♂ (male)"]
  J2 = double row male pin header, 8 pins [form="♂ (male)"]
  J3 = double row male pin header, 6 pins [form="♂ (male)"]
  IC1 = DIP - 8 pins [chip_label=AD627 package="DIP (Dual Inline) [THT]"]
  IC3 = MCP1700 [package=to-92]
  C1 = Tantalum Capacitor [capacitance=1μF package="100 mil [THT, tantalum]"]
  C2 = Tantalum Capacitor [capacitance=1μF package="100 mil [THT, tantalum]"]
  R1 = Resistor [tolerance=±5% resistance=51k package=THT]
  J5 = female pin header, 5 pins [form="♀ (female)"]
  J4 = female pin header, 5 pins [form="♀ (female)"]
  R3 = Resistor [tolerance=±1% resistance=270 package=THT]
  J6 = female pin header, 5 pins [form="♀ (female)"]
  J7 = female pin header, 5 pins [form="♀ (female)"]
  IC6 = DIP - 8 pins [chip_label=AD627 package="DIP (Dual Inline) [THT]"]
  IC7 = DIP - 16 pins [chip_label=MAX4617CPE package="DIP (Dual Inline) [THT]"]
  R5 = Resistor [tolerance=±5% resistance=51k package=THT]
  R6 = Resistor [tolerance=±5% resistance=750 package=THT]
  J8 = female pin header, 5 pins [form="♀ (female)"]
  J9 = female pin header, 5 pins [form="♀ (female)"]
  IC8 = DIP - 8 pins [chip_label=AD627 package="DIP (Dual Inline) [THT]"]
  R7 = Resistor [tolerance=±5% resistance=51k package=THT]
  R8 = Resistor [tolerance=±5% resistance=750 package=THT]
  IC5 = AZ432 [package=to-92]
  IC2 = DIP - 16 pins [chip_label=MAX4617CPE package="DIP (Dual Inline) [THT]"]
  IC9 = DIP - 16 pins [chip_label=MAX4617CPE package="DIP (Dual Inline) [THT]"]
  R4 = Resistor [tolerance=±5% resistance=750 package=THT]
  J10 = female pin header, 5 pins [form="♀ (female)"]
  J11 = female pin header, 5 pins [form="♀ (female)"]
  IC10 = DIP - 8 pins [chip_label=AD627 package="DIP (Dual Inline) [THT]"]
  IC11 = DIP - 16 pins [chip_label=MAX4617CPE package="DIP (Dual Inline) [THT]"]
  R9 = Resistor [tolerance=±5% resistance=51k package=THT]
  R10 = Resistor [tolerance=±5% resistance=750 package=THT]
  C7 = Ceramic Capacitor [capacitance=100nF package="100 mil [THT, multilayer]"]
  C8 = Ceramic Capacitor [capacitance=100nF package="100 mil [THT, multilayer]"]
  C9 = Ceramic Capacitor [capacitance=100nF package="100 mil [THT, multilayer]"]

nets:
  5V: J1.pin5, IC3.IN, C2.+
  GND: J1.pin6, IC1.-IN, IC1.-Vs, IC1.REF, IC3.GND, C1.-, C2.-, J5.pin5, J4.pin5, J6.pin5, J7.pin5, IC6.-IN, IC6.-Vs, IC6.REF, IC7.GND, J8.pin5, J9.pin5, IC8.-IN, IC8.-Vs, IC8.REF, IC5.A, IC2.GND, IC9.GND, J10.pin5, J11.pin5, IC10.-IN, IC10.-Vs, IC10.REF, IC11.GND, C7.1, C8.1, C9.1
  MUX_EN: J2.pin5, IC7.EN, IC2.EN, IC9.EN, IC11.EN
  MUX_A: J2.pin6, IC7.A, IC2.A, IC9.A, IC11.A
  MUX_B: J2.pin7, IC7.B, IC2.B, IC9.B, IC11.B
  MUX_C: J2.pin8, IC7.C, IC2.C, IC9.C, IC11.C
  ADC_CH0: J3.pin3, IC1.OUT
  ADC_CH1: J3.pin4, IC6.OUT
  ADC_CH2: J3.pin5, IC8.OUT
  N1: IC1.Rg#0, R1.Pin_0
  N2: IC1.+IN, IC2.X, R4.Pin_0
  3V3: IC1.+Vs, IC3.OUT, C1.+, R3.Pin_0, IC6.+Vs, IC7.VCC, IC8.+Vs, IC2.VCC, IC9.VCC, IC10.+Vs, IC11.VCC, C7.0, C8.0, C9.0
  N3: IC1.Rg#7, R1.Pin_1
  D2: J5.pin1, IC2.X4
  C2: J5.pin2, IC2.X6
  B2: J5.pin3, IC2.X7
  A2: J5.pin4, IC2.X5
  A1: J4.pin1, IC2.X2
  B1: J4.pin2, IC2.X1
  C1: J4.pin3, IC2.X0
  D1: J4.pin4, IC2.X3
  Vbias: R3.Pin_1, R6.Pin_1, IC5.REF, IC5.C
  A3: J6.pin1, IC7.X2
  B3: J6.pin2, IC7.X1
  C3: J6.pin3, IC7.X0
  D3: J6.pin4, IC7.X3
  E3: J7.pin1, IC7.X4
  C4: J7.pin2, IC7.X6
  B4: J7.pin3, IC7.X7
  A4: J7.pin4, IC7.X5
  N4: IC6.Rg#0, R5.Pin_0
  N5: IC6.+IN, IC7.X, R6.Pin_0
  N6: IC6.Rg#7, R5.Pin_1
  A6: J8.pin1, IC9.X2
  B6: J8.pin2, IC9.X1
  C6: J8.pin3, IC9.X0
  D6: J8.pin4, IC9.X3
  D5: J9.pin1, IC9.X4
  C5: J9.pin2, IC9.X6
  B5: J9.pin3, IC9.X7
  A5: J9.pin4, IC9.X5
  N7: IC8.Rg#0, R7.Pin_0
  N8: IC8.+IN, R8.Pin_0, IC9.X
  N9: IC8.Rg#7, R7.Pin_1
  N10: IC10.Rg#0, R9.Pin_0
  N11: IC10.+IN, IC11.X, R10.Pin_0
  ADC_CH3: IC10.OUT
  N12: IC10.Rg#7, R9.Pin_1

notes:
  VSHLD
  RESET
  5VO
  GND
  NC
  ADC_CH0
  ADC_CH1
  ADC_CH2
  ADC_CH3
  MUX_B
  MUX_C
  MUX_A

custom parts:
  DIP - 8 pins: A DIP stand-in part for whatever IC you want. With 8 pins on a 300mil dual inline package (DIP) footprint.
  DIP - 16 pins: A DIP stand-in part for whatever IC you want. With 16 pins on a 300mil dual inline package (DIP) footprint.
